# Fritzing sketch AgriSensor_Schematics (saved by Fritzing 0.9.6b)
breadboards: 2

parts:
  MH-ET_LIVE_ESP32_DEVKIT1 = MH-ET LIVE ESP32 DEVKIT 38 pins
  T1 = LM34 Temperature Sensor [package="TO92 [THT]"]
  ZS-042_RTC1 = ZS-042 RTC Module
  R1 = Resistor [tolerance=±5% power=0.25 resistance=220k package=THT]
  R2 = Resistor [tolerance=±5% power=0.25 resistance=330k package=THT]
  M1 = ph-4502c [package=THT]
  M2 = MT3608 Module
  Solar_Cell1 = 5V 100mA Polycrystalline PET Solar Cell [part_number=IM130407002]
  Solar_Cell2 = 5V 100mA Polycrystalline PET Solar Cell [part_number=IM130407002]
  TP1 = TP4056 [chip_label=TP4056 package="DIP (Dual Inline) [THT]"]
  18650_Lithium_Cell = 18650 battery holder [package=battery-18650-kit]
  M3 = MT3608 Module
  R5 = Resistor [tolerance=±5% power=0.25 resistance=220k package=THT]
  R6 = Resistor [tolerance=±5% power=0.25 resistance=330k package=THT]
  R7 = Resistor [tolerance=±5% power=0.25 resistance=220k package=THT]
  R8 = Resistor [tolerance=±5% power=0.25 resistance=330k package=THT]
  Capacitive_Soil_Moisture_Sensor1 = DFRobot Capacitive Soil Moisture Sensor V1.0 [part_number=SEN0193]
  Grove1 = Grove OLED 128x96

nets:
  VCC: MH-ET_LIVE_ESP32_DEVKIT1.3V3, T1.+Vs, ZS-042_RTC1.VCC, M2.pin2, Capacitive_Soil_Moisture_Sensor1.VCC, Grove1.VCC
  N1: MH-ET_LIVE_ESP32_DEVKIT1.IO34, R1.Pin_0, R2.Pin_0
  N2: MH-ET_LIVE_ESP32_DEVKIT1.IO32, Capacitive_Soil_Moisture_Sensor1.A
  N3: MH-ET_LIVE_ESP32_DEVKIT1.IO25, R5.Pin_1, R6.Pin_0
  N4: MH-ET_LIVE_ESP32_DEVKIT1.IO26, R7.Pin_1, R8.Pin_1
  GND: MH-ET_LIVE_ESP32_DEVKIT1.GND#58, T1.GND, ZS-042_RTC1.GND, R2.Pin_1, M2.pin1, M3.pin4, R6.Pin_1, R8.Pin_0, Capacitive_Soil_Moisture_Sensor1.GND, Grove1.GND
  N5: MH-ET_LIVE_ESP32_DEVKIT1.5V, M3.pin3
  N6: MH-ET_LIVE_ESP32_DEVKIT1.IO22, ZS-042_RTC1.SCL, Grove1.SCL
  N7: MH-ET_LIVE_ESP32_DEVKIT1.IO21, ZS-042_RTC1.SDA, Grove1.SDA
  N8: MH-ET_LIVE_ESP32_DEVKIT1.IO17, T1.Vout
  N9: R1.Pin_1, M1.pin3
  N10: M1.pin5, M2.pin4
  N11: M1.pin6, M2.pin3
  GND_2: Solar_Cell1.GND, Solar_Cell2.GND, TP1.pin2
  5V: Solar_Cell1.5V, Solar_Cell2.5V, TP1.pin1, R7.Pin_0
  N12: TP1.pin3, M3.pin2
  N13: TP1.pin4, 18650_Lithium_Cell.-, R5.Pin_0
  N14: TP1.pin5, 18650_Lithium_Cell.+
  N15: TP1.pin6, M3.pin1

custom parts:
  MH-ET LIVE ESP32 DEVKIT 38 pins: http://mh.nodebb.com/topic/2/mh-et-live-esp32-devkit
  ph-4502c: ph-4502c PH Meter.
  MT3608 Module: MT3608 Boost Converter Module Links: Aerosemi MT3608 2A Step Up Converter datasheet
  5V 100mA Polycrystalline PET Solar Cell: This is 5V 100mA Polycrystalline PET Solar Cell. It is high quality and exquisite appearance. It is used in all kinds of high-grade electronic products.
  TP4056: A DIP stand-in part for whatever IC you want. With 6 pins on a 300mil dual inline package (DIP) footprint.
  18650 battery holder: 18650 Battery
  DFRobot Capacitive Soil Moisture Sensor V1.0: DFRobot Capacitive Soil Moisture Sensor V1.0 This product measures soil moisture levels by capacitive sensing, rather than resistive sensing like other types of moisture sensor. It is made of a corrosion resistant material giving it a long service life. Insert it into soil and impress your friends with the real-time soil moisture data! The product includes an on-board voltage regulator which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
