# Fritzing sketch AgriSensor_Schematics (saved by Fritzing 0.9.9b)
breadboards: 2

parts:
  MH-ET_LIVE_ESP32_DEVKIT1 = MH-ET LIVE ESP32 DEVKIT 38 pins
  T1 = LM34 Temperature Sensor [package="TO92 [THT]"]
  Part1 = Soil Moisture Sensor

nets:
  3V3: MH-ET_LIVE_ESP32_DEVKIT1.3V3, T1.+Vs, Part1.VCC
  N1: MH-ET_LIVE_ESP32_DEVKIT1.IO32, Part1.SIG
  GND: MH-ET_LIVE_ESP32_DEVKIT1.GND#58, T1.GND, Part1.GND
  N2: MH-ET_LIVE_ESP32_DEVKIT1.IO17, T1.Vout

custom parts:
  MH-ET LIVE ESP32 DEVKIT 38 pins: http://mh.nodebb.com/topic/2/mh-et-live-esp32-devkit
